// Logisim project 735576-multi.circ as structural Verilog: 3 circuits, main circuit PROC
module BR4 (
  input  reset,
  input  [1:0] RA,
  input  RegWr,
  input  [1:0] RW,
  input  [1:0] RB,
  input  [31:0] busW,
  input  reloj,
  output [31:0] BusA,
  output [31:0] BusB
);

  wire and_1_out, and_2_out, and_3_out, and_4_out, decoder_1_out0, decoder_1_out1, decoder_1_out2,
       decoder_1_out3;
  wire [31:0] register_1_q, register_2_q, register_3_q, register_4_q;

  Decoder #(.select(2), .disabled(0), .enable("false")) decoder_1 (
    .out0(decoder_1_out0), .out1(decoder_1_out1), .out2(decoder_1_out2), .out3(decoder_1_out3), .sel(RW));
  and and_1 (and_1_out, RegWr, decoder_1_out0);
  and and_2 (and_2_out, RegWr, decoder_1_out1);
  and and_3 (and_3_out, RegWr, decoder_1_out2);
  and and_4 (and_4_out, RegWr, decoder_1_out3);
  Register #(.width(32)) register_1 (.D(busW), .en(and_1_out), .Q(register_1_q), .clk(reloj), .clr(reset));
  Register #(.width(32)) register_2 (.D(busW), .en(and_2_out), .Q(register_2_q), .clk(reloj), .clr(reset));
  Register #(.width(32)) register_3 (.D(busW), .en(and_3_out), .Q(register_3_q), .clk(reloj), .clr(reset));
  Register #(.width(32)) register_4 (.D(busW), .en(and_4_out), .Q(register_4_q), .clk(reloj), .clr(reset));
  Multiplexer #(.select(2), .width(32), .enable("false")) multiplexer_1 (
    .in0(register_1_q), .in1(register_2_q), .in2(register_3_q), .in3(register_4_q), .out(BusA), .sel(RA));
  Multiplexer #(.select(2), .width(32), .enable("false")) multiplexer_2 (
    .in0(register_1_q), .in1(register_2_q), .in2(register_3_q), .in3(register_4_q), .out(BusB), .sel(RB));
endmodule

module BR32 (
  input  [4:0] RA,
  input  [4:0] RB,
  input  reset,
  input  RegW,
  input  [4:0] RW,
  input  [31:0] busW,
  input  reloj,
  output [31:0] busA,
  output [31:0] busB
);

  wire and_1_out, and_2_out, and_3_out, and_4_out, and_5_out, and_6_out, and_7_out, and_8_out,
       decoder_1_out0, decoder_1_out1, decoder_1_out2, decoder_1_out3, decoder_1_out4, decoder_1_out5,
       decoder_1_out6, decoder_1_out7;
  wire [31:0] br4_1_busa, br4_1_busb, br4_2_busa, br4_2_busb, br4_3_busa, br4_3_busb, br4_4_busa, br4_4_busb,
       br4_5_busa, br4_5_busb, br4_6_busa, br4_6_busb, br4_7_busa, br4_7_busb, br4_8_busa, br4_8_busb;

  Decoder #(.select(3), .disabled(0), .enable("false")) decoder_1 (
    .out0(decoder_1_out0), .out1(decoder_1_out1), .out2(decoder_1_out2), .out3(decoder_1_out3),
    .out4(decoder_1_out4), .out5(decoder_1_out5), .out6(decoder_1_out6), .out7(decoder_1_out7), .sel(RW[4:2]));
  and and_1 (and_1_out, decoder_1_out0, RegW);
  and and_2 (and_2_out, decoder_1_out1, RegW);
  and and_3 (and_3_out, decoder_1_out2, RegW);
  and and_4 (and_4_out, decoder_1_out3, RegW);
  and and_5 (and_5_out, decoder_1_out4, RegW);
  and and_6 (and_6_out, decoder_1_out5, RegW);
  and and_7 (and_7_out, decoder_1_out6, RegW);
  and and_8 (and_8_out, decoder_1_out7, RegW);
  BR4 br4_1 (
    .BusA(br4_1_busa), .BusB(br4_1_busb), .RegWr(and_1_out), .RW(RW[1:0]), .busW(busW), .reset(reset),
    .RA(RA[1:0]), .RB(RB[1:0]), .reloj(reloj));
  BR4 br4_2 (
    .BusA(br4_2_busa), .BusB(br4_2_busb), .RegWr(and_2_out), .RW(RW[1:0]), .busW(busW), .reset(reset),
    .RA(RA[1:0]), .RB(RB[1:0]), .reloj(reloj));
  BR4 br4_3 (
    .BusA(br4_3_busa), .BusB(br4_3_busb), .RegWr(and_3_out), .RW(RW[1:0]), .busW(busW), .reset(reset),
    .RA(RA[1:0]), .RB(RB[1:0]), .reloj(reloj));
  BR4 br4_4 (
    .BusA(br4_4_busa), .BusB(br4_4_busb), .RegWr(and_4_out), .RW(RW[1:0]), .busW(busW), .reset(reset),
    .RA(RA[1:0]), .RB(RB[1:0]), .reloj(reloj));
  BR4 br4_5 (
    .BusA(br4_5_busa), .BusB(br4_5_busb), .RegWr(and_5_out), .RW(RW[1:0]), .busW(busW), .reset(reset),
    .RA(RA[1:0]), .RB(RB[1:0]), .reloj(reloj));
  BR4 br4_6 (
    .BusA(br4_6_busa), .BusB(br4_6_busb), .RegWr(and_6_out), .RW(RW[1:0]), .busW(busW), .reset(reset),
    .RA(RA[1:0]), .RB(RB[1:0]), .reloj(reloj));
  BR4 br4_7 (
    .BusA(br4_7_busa), .BusB(br4_7_busb), .RegWr(and_7_out), .RW(RW[1:0]), .busW(busW), .reset(reset),
    .RA(RA[1:0]), .RB(RB[1:0]), .reloj(reloj));
  BR4 br4_8 (
    .BusA(br4_8_busa), .BusB(br4_8_busb), .RegWr(and_8_out), .RW(RW[1:0]), .busW(busW), .reset(reset),
    .RA(RA[1:0]), .RB(RB[1:0]), .reloj(reloj));
  Multiplexer #(.select(3), .width(32), .enable("false")) multiplexer_1 (
    .in0(br4_1_busa), .in1(br4_2_busa), .in2(br4_3_busa), .in3(br4_4_busa), .in4(br4_5_busa),
    .in5(br4_6_busa), .in6(br4_7_busa), .in7(br4_8_busa), .out(busA), .sel(RA[4:2]));
  Multiplexer #(.select(3), .width(32), .enable("false")) multiplexer_2 (
    .in0(br4_1_busb), .in1(br4_2_busb), .in2(br4_3_busb), .in3(br4_4_busb), .in4(br4_5_busb),
    .in5(br4_6_busb), .in6(br4_7_busb), .in7(br4_8_busb), .out(busB), .sel(RB[4:2]));
endmodule

module PROC (
  input  in_1
);

  wire mux, op, pc, ra_t, rb_t, rc, regWrite, reloj;
  wire [1:0] register_1_q, rom_2_data;
  wire [3:0] counter_1_q;
  wire [4:0] RA, RB, RW;
  wire [5:0] NADA;
  wire [31:0] adder_1_out, bit_extender_1_out, br32_1_busa, br32_1_busb, multiplexer_1_out, RA_q, RB_q, RC_q;

  Clock clock_1 (.out(reloj));
  Counter #(.width(4), .max('ha), .ongoal("stay")) counter_1 (
    .Q(counter_1_q), .clk(pc), .clr(in_1));  // open: load, D, count, carry
  Register #(.width(2)) register_1 (.D(rom_2_data), .Q(register_1_q), .clk(reloj), .clr(in_1));  // open: en
  ROM #(.addrWidth(4), .dataWidth(22)) rom_1 (.addr(counter_1_q), .data({op, NADA, RA, RB, RW}));  // open: sel
  ROM #(.addrWidth(3), .dataWidth(2)) rom_2 (.addr({register_1_q, op}), .data(rom_2_data));  // open: sel
  assign bit_extender_1_out = {{16{1'b0}}, {NADA, RA, RB}};  // Bit_Extender bit_extender_1
  Multiplexer #(.width(32), .enable("false")) multiplexer_1 (
    .in0(bit_extender_1_out), .in1(RC_q), .out(multiplexer_1_out), .sel(mux));
  ROM #(.addrWidth(2), .dataWidth(6)) rom_3 (
    .addr(register_1_q), .data({ra_t, rb_t, rc, regWrite, mux, pc}));  // open: sel
  BR32 br32_1 (
    .RA(RA), .RB(RB), .RegW(regWrite), .RW(RW), .busW(multiplexer_1_out), .busA(br32_1_busa),
    .busB(br32_1_busb), .reset(in_1), .reloj(reloj));
  Register #(.width(32)) u_RA (.D(br32_1_busa), .en(ra_t), .Q(RA_q), .clk(reloj), .clr(in_1));
  Register #(.width(32)) u_RB (.D(br32_1_busb), .en(rb_t), .Q(RB_q), .clk(reloj), .clr(in_1));
  // Probe on RB_q
  // Probe on RA_q
  Adder #(.width(32)) adder_1 (.a(RA_q), .b(RB_q), .out(adder_1_out));  // open: cin, cout
  // Probe on RC_q
  Register #(.width(32)) u_RC (.D(adder_1_out), .en(rc), .Q(RC_q), .clk(reloj), .clr(in_1));

  // Other names for the same wires on the sheet: reset = in_1

  // Notes on the sheet:
  //   contents of rom_1 (hex, n*v repeats v):
  //   e0 61 a2 a3 e4 c5 200026 200867 2010a8 2018e7 201d06
  //   contents of rom_2 (hex, n*v repeats v):
  //   1 1 2 3 0 0 2 2
  //   contents of rom_3 (hex, n*v repeats v):
  //   30 c 1 6
endmodule
