// Logisim project 735576-multi2.circ as structural Verilog: 3 circuits, main circuit PROC
module BR4 (
  input  reset,
  input  [1:0] RA,
  input  RegWr,
  input  [1:0] RW,
  input  [1:0] RB,
  input  [31:0] busW,
  input  reloj,
  output [31:0] BusA,
  output [31:0] BusB
);

  wire and_1_out, and_2_out, and_3_out, and_4_out, decoder_1_out0, decoder_1_out1, decoder_1_out2,
       decoder_1_out3;
  wire [31:0] register_1_q, register_2_q, register_3_q, register_4_q;

  Decoder #(.select(2), .disabled(0), .enable("false")) decoder_1 (
    .out0(decoder_1_out0), .out1(decoder_1_out1), .out2(decoder_1_out2), .out3(decoder_1_out3), .sel(RW));
  and and_1 (and_1_out, RegWr, decoder_1_out0);
  and and_2 (and_2_out, RegWr, decoder_1_out1);
  and and_3 (and_3_out, RegWr, decoder_1_out2);
  and and_4 (and_4_out, RegWr, decoder_1_out3);
  Register #(.width(32)) register_1 (.D(busW), .en(and_1_out), .Q(register_1_q), .clk(reloj), .clr(reset));
  Register #(.width(32)) register_2 (.D(busW), .en(and_2_out), .Q(register_2_q), .clk(reloj), .clr(reset));
  Register #(.width(32)) register_3 (.D(busW), .en(and_3_out), .Q(register_3_q), .clk(reloj), .clr(reset));
  Register #(.width(32)) register_4 (.D(busW), .en(and_4_out), .Q(register_4_q), .clk(reloj), .clr(reset));
  Multiplexer #(.select(2), .width(32), .enable("false")) multiplexer_1 (
    .in0(register_1_q), .in1(register_2_q), .in2(register_3_q), .in3(register_4_q), .out(BusA), .sel(RA));
  Multiplexer #(.select(2), .width(32), .enable("false")) multiplexer_2 (
    .in0(register_1_q), .in1(register_2_q), .in2(register_3_q), .in3(register_4_q), .out(BusB), .sel(RB));
endmodule

module BR32 (
  input  [4:0] RA,
  input  [4:0] RB,
  input  reset,
  input  RegW,
  input  [4:0] RW,
  input  [31:0] busW,
  input  reloj,
  output [31:0] busA,
  output [31:0] busB
);

  wire and_1_out, and_2_out, and_3_out, and_4_out, and_5_out, and_6_out, and_7_out, and_8_out,
       decoder_1_out0, decoder_1_out1, decoder_1_out2, decoder_1_out3, decoder_1_out4, decoder_1_out5,
       decoder_1_out6, decoder_1_out7;
  wire [31:0] br4_1_busa, br4_1_busb, br4_2_busa, br4_2_busb, br4_3_busa, br4_3_busb, br4_4_busa, br4_4_busb,
       br4_5_busa, br4_5_busb, br4_6_busa, br4_6_busb, br4_7_busa, br4_7_busb, br4_8_busa, br4_8_busb;

  Decoder #(.select(3), .disabled(0), .enable("false")) decoder_1 (
    .out0(decoder_1_out0), .out1(decoder_1_out1), .out2(decoder_1_out2), .out3(decoder_1_out3),
    .out4(decoder_1_out4), .out5(decoder_1_out5), .out6(decoder_1_out6), .out7(decoder_1_out7), .sel(RW[4:2]));
  and and_1 (and_1_out, decoder_1_out0, RegW);
  and and_2 (and_2_out, decoder_1_out1, RegW);
  and and_3 (and_3_out, decoder_1_out2, RegW);
  and and_4 (and_4_out, decoder_1_out3, RegW);
  and and_5 (and_5_out, decoder_1_out4, RegW);
  and and_6 (and_6_out, decoder_1_out5, RegW);
  and and_7 (and_7_out, decoder_1_out6, RegW);
  and and_8 (and_8_out, decoder_1_out7, RegW);
  BR4 br4_1 (
    .BusA(br4_1_busa), .BusB(br4_1_busb), .RegWr(and_1_out), .RW(RW[1:0]), .busW(busW), .reset(reset),
    .RA(RA[1:0]), .RB(RB[1:0]), .reloj(reloj));
  BR4 br4_2 (
    .BusA(br4_2_busa), .BusB(br4_2_busb), .RegWr(and_2_out), .RW(RW[1:0]), .busW(busW), .reset(reset),
    .RA(RA[1:0]), .RB(RB[1:0]), .reloj(reloj));
  BR4 br4_3 (
    .BusA(br4_3_busa), .BusB(br4_3_busb), .RegWr(and_3_out), .RW(RW[1:0]), .busW(busW), .reset(reset),
    .RA(RA[1:0]), .RB(RB[1:0]), .reloj(reloj));
  BR4 br4_4 (
    .BusA(br4_4_busa), .BusB(br4_4_busb), .RegWr(and_4_out), .RW(RW[1:0]), .busW(busW), .reset(reset),
    .RA(RA[1:0]), .RB(RB[1:0]), .reloj(reloj));
  BR4 br4_5 (
    .BusA(br4_5_busa), .BusB(br4_5_busb), .RegWr(and_5_out), .RW(RW[1:0]), .busW(busW), .reset(reset),
    .RA(RA[1:0]), .RB(RB[1:0]), .reloj(reloj));
  BR4 br4_6 (
    .BusA(br4_6_busa), .BusB(br4_6_busb), .RegWr(and_6_out), .RW(RW[1:0]), .busW(busW), .reset(reset),
    .RA(RA[1:0]), .RB(RB[1:0]), .reloj(reloj));
  BR4 br4_7 (
    .BusA(br4_7_busa), .BusB(br4_7_busb), .RegWr(and_7_out), .RW(RW[1:0]), .busW(busW), .reset(reset),
    .RA(RA[1:0]), .RB(RB[1:0]), .reloj(reloj));
  BR4 br4_8 (
    .BusA(br4_8_busa), .BusB(br4_8_busb), .RegWr(and_8_out), .RW(RW[1:0]), .busW(busW), .reset(reset),
    .RA(RA[1:0]), .RB(RB[1:0]), .reloj(reloj));
  Multiplexer #(.select(3), .width(32), .enable("false")) multiplexer_1 (
    .in0(br4_1_busa), .in1(br4_2_busa), .in2(br4_3_busa), .in3(br4_4_busa), .in4(br4_5_busa),
    .in5(br4_6_busa), .in6(br4_7_busa), .in7(br4_8_busa), .out(busA), .sel(RA[4:2]));
  Multiplexer #(.select(3), .width(32), .enable("false")) multiplexer_2 (
    .in0(br4_1_busb), .in1(br4_2_busb), .in2(br4_3_busb), .in3(br4_4_busb), .in4(br4_5_busb),
    .in5(br4_6_busb), .in6(br4_7_busb), .in7(br4_8_busb), .out(busB), .sel(RB[4:2]));
endmodule

module PROC (
  input  in_1
);

  wire aluwrite, awrite, branch, bwrite, en, irwrite, mdrwrite, muxb, muxpc, not_2_out, pcwrite, ram,
       regWrite, reloj, tty_ctrl_1_p1, zero;
  wire [1:0] muxw;
  wire [2:0] op;
  wire [3:0] register_2_q, rom_2_data;
  wire [4:0] multiplexer_2_out, RA, RB, RW;
  wire [15:0] adder_1_out, multiplexer_1_out, register_1_q;
  wire [28:15] IR_q;
  wire [31:0] A, adder_2_out, bit_extender_1_out, br32_1_busb, D, MDR_q, multiplexer_3_out, RA_q, ram_1_data,
       RC_q, rom_1_data;

  // Probe on multiplexer_1_out
  Adder #(.width(16)) adder_1 (.a(register_1_q), .b(16'h1), .out(adder_1_out));  // open: cin, cout
  Multiplexer #(.width(16), .enable("false")) multiplexer_1 (
    .in0(adder_1_out), .in1({IR_q, RW[4:3]}), .out(multiplexer_1_out), .sel(muxpc));
  Register #(.width(16)) register_1 (.D(multiplexer_1_out), .Q(register_1_q), .clk(pcwrite), .clr(in_1));  // open: en
  Register #(.width(4)) register_2 (.D(rom_2_data), .Q(register_2_q), .clk(reloj), .clr(in_1));  // open: en
  // Probe on op
  ROM #(.addrWidth(16), .dataWidth(32)) rom_1 (.addr(register_1_q), .data(rom_1_data));  // open: sel
  ROM #(.addrWidth(7), .dataWidth(4)) rom_2 (.addr({op, register_2_q}), .data(rom_2_data));  // open: sel
  Register #(.width(32)) IR (.D(rom_1_data), .en(irwrite), .Q({op, IR_q, RW, RB, RA}), .clk(reloj), .clr(in_1));
  // tty_ctrl tty_ctrl_1: pin names not known; wires that end beside it: tty_ctrl_1_p1, tty_ctrl_1_p1
  // TTY tty_1: pin names not known; wires that end beside it: A[15:0], en, D[6:0], reloj, tty_ctrl_1_p1
  and and_1 (muxpc, zero, branch);
  Clock clock_1 (.out(reloj));
  // Probe on {IR_q, RW[4:3]}
  ROM #(.addrWidth(5), .dataWidth(12)) rom_3 (
    .addr({zero, rom_2_data}),
    .data({branch, pcwrite, irwrite, awrite, bwrite, muxb, regWrite, muxw, aluwrite, ram, mdrwrite}));  // open: sel
  Multiplexer #(.width(5), .enable("false")) multiplexer_2 (.in0(RB), .in1(RW), .out(multiplexer_2_out), .sel(muxb));
  // Probe on multiplexer_3_out
  assign bit_extender_1_out = {{16{1'b0}}, {IR_q, RW[4:3]}};  // Bit_Extender bit_extender_1
  not not_1 (en, ram);
  Multiplexer #(.select(2), .width(32), .enable("false")) multiplexer_3 (
    .in0(bit_extender_1_out), .in1(RC_q), .in2(MDR_q), .out(multiplexer_3_out), .sel(muxw));  // open: in3
  // Probe on muxw
  // Probe on RA
  BR32 br32_1 (
    .RA(RA), .RB(RB), .RegW(regWrite), .RW(multiplexer_2_out), .busW(multiplexer_3_out), .busA(A),
    .busB(br32_1_busb), .reset(in_1), .reloj(reloj));
  // Probe on A
  // Probe on br32_1_busb
  Register #(.width(32)) u_RA (.D(A), .en(awrite), .Q(RA_q), .clk(reloj), .clr(in_1));
  Comparator #(.width(32)) comparator_1 (.a(RA_q), .b(D), .eq(zero));  // open: gt, lt
  Register #(.width(32)) u_RB (.D(br32_1_busb), .en(bwrite), .Q(D), .clk(reloj), .clr(in_1));
  // Probe on MDR_q
  // Probe on D
  // Probe on RA_q
  Register #(.width(32)) RC (.D(adder_2_out), .en(aluwrite), .Q(RC_q), .clk(reloj), .clr(in_1));
  Adder #(.width(32)) adder_2 (.a(RA_q), .b(D), .out(adder_2_out));  // open: cin, cout
  // Probe on RC_q
  not not_2 (not_2_out, ram);
  RAM #(.addrWidth(16), .dataWidth(32), .bus("separate")) ram_1 (
    .addr(A[15:0]), .din(D), .data(ram_1_data), .str(not_2_out), .clk(reloj), .ld(ram), .clr(in_1));  // open: sel
  Register #(.width(32)) MDR (.D(ram_1_data), .en(mdrwrite), .Q(MDR_q), .clk(reloj), .clr(in_1));

  // Other names for the same wires on the sheet: reset = in_1

  // Notes on the sheet:
  //   contents of rom_1 (hex, n*v repeats v):
  //   a00000a0 a000c000 a0000020 a0000040 a0002060 a00420c0 20000843 40000082 200014a4 20000423 80018020
  //   8000c000 a0000000 600000a0 bfffe020 a009e040 a0096060 8002e0c5 a009c080 a00400a0 60000081 60000041
  //   600000a1 60000041 60000061
  //   contents of rom_2 (hex, n*v repeats v):
  //   d 15*0 2 0 3 4 12*0 5 4*0 6 7 9*0 8 7*0 9 7*0 a 9*0 b c 4*0 1 31*0 f
  //   código ASCII 7 bits a imprimir en tty (0 borra pantalla)
  //   contents of rom_3 (hex, n*v repeats v):
  //   602 22 182 6 2a 82 3 32 182 0 182 802 2 2 0 2 602 22 182 6 2a 82 3 32 182 0 182 802 c02 0 0 402
endmodule
