// Logisim project 735576-segR.circ as structural Verilog: 3 circuits, main circuit PROC
module BR4 (
  input  reset,
  input  [1:0] RA,
  input  RegWr,
  input  [1:0] RW,
  input  [1:0] RB,
  input  [31:0] busW,
  input  reloj,
  output [31:0] BusA,
  output [31:0] BusB
);

  wire and_1_out, and_2_out, and_3_out, and_4_out, decoder_1_out0, decoder_1_out1, decoder_1_out2,
       decoder_1_out3;
  wire [31:0] register_1_q, register_2_q, register_3_q, register_4_q;

  Decoder #(.select(2), .disabled(0), .enable("false")) decoder_1 (
    .out0(decoder_1_out0), .out1(decoder_1_out1), .out2(decoder_1_out2), .out3(decoder_1_out3), .sel(RW));
  and and_1 (and_1_out, RegWr, decoder_1_out0);
  and and_2 (and_2_out, RegWr, decoder_1_out1);
  and and_3 (and_3_out, RegWr, decoder_1_out2);
  and and_4 (and_4_out, RegWr, decoder_1_out3);
  Register #(.width(32)) register_1 (.D(busW), .en(and_1_out), .Q(register_1_q), .clk(reloj), .clr(reset));
  Register #(.width(32)) register_2 (.D(busW), .en(and_2_out), .Q(register_2_q), .clk(reloj), .clr(reset));
  Register #(.width(32)) register_3 (.D(busW), .en(and_3_out), .Q(register_3_q), .clk(reloj), .clr(reset));
  Register #(.width(32)) register_4 (.D(busW), .en(and_4_out), .Q(register_4_q), .clk(reloj), .clr(reset));
  Multiplexer #(.select(2), .width(32), .enable("false")) multiplexer_1 (
    .in0(register_1_q), .in1(register_2_q), .in2(register_3_q), .in3(register_4_q), .out(BusA), .sel(RA));
  Multiplexer #(.select(2), .width(32), .enable("false")) multiplexer_2 (
    .in0(register_1_q), .in1(register_2_q), .in2(register_3_q), .in3(register_4_q), .out(BusB), .sel(RB));
endmodule

module BR32 (
  input  [4:0] RA,
  input  [4:0] RB,
  input  reset,
  input  RegW,
  input  [4:0] RW,
  input  [31:0] busW,
  input  reloj,
  output [31:0] busA,
  output [31:0] busB
);

  wire and_1_out, and_2_out, and_3_out, and_4_out, and_5_out, and_6_out, and_7_out, and_8_out,
       decoder_1_out0, decoder_1_out1, decoder_1_out2, decoder_1_out3, decoder_1_out4, decoder_1_out5,
       decoder_1_out6, decoder_1_out7;
  wire [31:0] br4_1_busa, br4_1_busb, br4_2_busa, br4_2_busb, br4_3_busa, br4_3_busb, br4_4_busa, br4_4_busb,
       br4_5_busa, br4_5_busb, br4_6_busa, br4_6_busb, br4_7_busa, br4_7_busb, br4_8_busa, br4_8_busb;

  Decoder #(.select(3), .disabled(0), .enable("false")) decoder_1 (
    .out0(decoder_1_out0), .out1(decoder_1_out1), .out2(decoder_1_out2), .out3(decoder_1_out3),
    .out4(decoder_1_out4), .out5(decoder_1_out5), .out6(decoder_1_out6), .out7(decoder_1_out7), .sel(RW[4:2]));
  and and_1 (and_1_out, decoder_1_out0, RegW);
  and and_2 (and_2_out, decoder_1_out1, RegW);
  and and_3 (and_3_out, decoder_1_out2, RegW);
  and and_4 (and_4_out, decoder_1_out3, RegW);
  and and_5 (and_5_out, decoder_1_out4, RegW);
  and and_6 (and_6_out, decoder_1_out5, RegW);
  and and_7 (and_7_out, decoder_1_out6, RegW);
  and and_8 (and_8_out, decoder_1_out7, RegW);
  BR4 br4_1 (
    .BusA(br4_1_busa), .BusB(br4_1_busb), .RegWr(and_1_out), .RW(RW[1:0]), .busW(busW), .reset(reset),
    .RA(RA[1:0]), .RB(RB[1:0]), .reloj(reloj));
  BR4 br4_2 (
    .BusA(br4_2_busa), .BusB(br4_2_busb), .RegWr(and_2_out), .RW(RW[1:0]), .busW(busW), .reset(reset),
    .RA(RA[1:0]), .RB(RB[1:0]), .reloj(reloj));
  BR4 br4_3 (
    .BusA(br4_3_busa), .BusB(br4_3_busb), .RegWr(and_3_out), .RW(RW[1:0]), .busW(busW), .reset(reset),
    .RA(RA[1:0]), .RB(RB[1:0]), .reloj(reloj));
  BR4 br4_4 (
    .BusA(br4_4_busa), .BusB(br4_4_busb), .RegWr(and_4_out), .RW(RW[1:0]), .busW(busW), .reset(reset),
    .RA(RA[1:0]), .RB(RB[1:0]), .reloj(reloj));
  BR4 br4_5 (
    .BusA(br4_5_busa), .BusB(br4_5_busb), .RegWr(and_5_out), .RW(RW[1:0]), .busW(busW), .reset(reset),
    .RA(RA[1:0]), .RB(RB[1:0]), .reloj(reloj));
  BR4 br4_6 (
    .BusA(br4_6_busa), .BusB(br4_6_busb), .RegWr(and_6_out), .RW(RW[1:0]), .busW(busW), .reset(reset),
    .RA(RA[1:0]), .RB(RB[1:0]), .reloj(reloj));
  BR4 br4_7 (
    .BusA(br4_7_busa), .BusB(br4_7_busb), .RegWr(and_7_out), .RW(RW[1:0]), .busW(busW), .reset(reset),
    .RA(RA[1:0]), .RB(RB[1:0]), .reloj(reloj));
  BR4 br4_8 (
    .BusA(br4_8_busa), .BusB(br4_8_busb), .RegWr(and_8_out), .RW(RW[1:0]), .busW(busW), .reset(reset),
    .RA(RA[1:0]), .RB(RB[1:0]), .reloj(reloj));
  Multiplexer #(.select(3), .width(32), .enable("false")) multiplexer_1 (
    .in0(br4_1_busa), .in1(br4_2_busa), .in2(br4_3_busa), .in3(br4_4_busa), .in4(br4_5_busa),
    .in5(br4_6_busa), .in6(br4_7_busa), .in7(br4_8_busa), .out(busA), .sel(RA[4:2]));
  Multiplexer #(.select(3), .width(32), .enable("false")) multiplexer_2 (
    .in0(br4_1_busb), .in1(br4_2_busb), .in2(br4_3_busb), .in3(br4_4_busb), .in4(br4_5_busb),
    .in5(br4_6_busb), .in6(br4_7_busb), .in7(br4_8_busb), .out(busB), .sel(RB[4:2]));
endmodule

module PROC (
  input  in_1
);

  wire aluw, aluwrite, and_2_out, and_3_out, awrite, branch, bwrite, en, irwrite, mdrwrite, muxa, muxb,
       muxpc, noRW, not_2_out, not_3_out, not_4_out, or_1_out, PC, pcwrite, ram, register_2_q, register_3_q,
       register_4_q, register_5_q, register_9_q, register_12_q, RegW, regWrite, reloj, RM, tty_ctrl_1_p1,
       zero;
  wire [1:0] muxw, MX, register_7_q, register_15_q;
  wire [2:0] op;
  wire [4:0] B, ES, ES_2_q, ES_q, multiplexer_2_out, RA, RB, register_8_q, register_16_q, RW;
  wire [15:0] a_t, adder_1_out, multiplexer_1_out, register_1_q;
  wire [28:15] IR_q;
  wire [31:0] A, adder_2_out, ALU, bit_extender_1_out, br32_1_busa, br32_1_busb, D, d_t, IM_2_q, IM_q, INM,
       multiplexer_3_out, ram_1_data, RC_q, rom_1_data;

  Adder #(.width(16)) adder_1 (.a(register_1_q), .b(16'h1), .out(adder_1_out));  // open: cin, cout
  // Probe on multiplexer_1_out
  Multiplexer #(.width(16), .enable("false")) multiplexer_1 (
    .in0(adder_1_out), .in1(INM[15:0]), .out(multiplexer_1_out), .sel(muxpc));
  // Probe on muxpc
  Register #(.width(16)) register_1 (.D(multiplexer_1_out), .Q(register_1_q), .clk(reloj), .clr(in_1));  // open: en
  // Probe on op
  ROM #(.addrWidth(16), .dataWidth(32)) rom_1 (.addr(register_1_q), .data(rom_1_data));  // open: sel
  Register #(.width(32)) IR (.D(rom_1_data), .en(irwrite), .Q({op, IR_q, RW, RB, RA}), .clk(reloj), .clr(in_1));
  ROM #(.addrWidth(4), .dataWidth(12)) rom_2 (
    .addr({op, zero}),
    .data({branch, pcwrite, irwrite, awrite, bwrite, muxa, regWrite, muxw, aluwrite, ram, mdrwrite}));  // open: sel
  // tty_ctrl tty_ctrl_1: pin names not known; wires that end beside it: tty_ctrl_1_p1, tty_ctrl_1_p1
  // TTY tty_1: pin names not known; wires that end beside it: a_t, en, d_t[6:0], reloj, tty_ctrl_1_p1
  and and_1 (PC, zero, branch);
  // Probe on {IR_q, RW[4:3]}
  assign bit_extender_1_out = {{16{1'b0}}, {IR_q, RW[4:3]}};  // Bit_Extender bit_extender_1
  // Probe on muxw
  // Probe on multiplexer_2_out
  Multiplexer #(.width(5), .enable("false")) multiplexer_2 (.in0(B), .in1(ES), .out(multiplexer_2_out), .sel(muxb));
  // Probe on multiplexer_3_out
  not not_1 (en, RM);
  // Probe on RA
  Multiplexer #(.select(2), .width(32), .enable("false")) multiplexer_3 (
    .in0(INM), .in1(ALU), .in2(ram_1_data), .out(multiplexer_3_out), .sel(MX));  // open: in3
  // Probe on MX
  or or_1 (or_1_out, noRW, muxpc);
  BR32 br32_1 (
    .RA(RA), .RB(RB), .RegW(RegW), .RW(multiplexer_2_out), .busW(multiplexer_3_out), .busA(br32_1_busa),
    .busB(br32_1_busb), .reset(in_1), .reloj(reloj));
  Clock clock_1 (.out(reloj));
  not not_2 (not_2_out, or_1_out);
  and and_2 (and_2_out, PC, not_3_out);
  not not_3 (not_3_out, noRW);
  // Probe on br32_1_busa
  Comparator #(.width(32)) comparator_1 (.a(br32_1_busa), .b(br32_1_busb), .eq(zero));  // open: gt, lt
  // Probe on br32_1_busb
  and and_3 (and_3_out, regWrite, not_2_out);
  // Probe on RW
  // Probe on RB
  Register #(.width(1)) register_2 (.D(and_3_out), .Q(register_2_q), .clk(reloj), .clr(in_1));  // open: en
  Register #(.width(1)) register_3 (.D(and_2_out), .Q(register_3_q), .clk(reloj), .clr(in_1));  // open: en
  Register #(.width(1)) register_4 (.D(ram), .Q(register_4_q), .clk(reloj), .clr(in_1));  // open: en
  Register #(.width(1)) register_5 (.D(muxa), .Q(register_5_q), .clk(reloj), .clr(in_1));  // open: en
  Register #(.width(1)) register_6 (.D(aluwrite), .Q(aluw), .clk(reloj), .clr(in_1));  // open: en
  Register #(.width(32)) u_RA (.D(br32_1_busa), .en(awrite), .Q(A), .clk(reloj), .clr(in_1));
  Register #(.width(32)) u_RB (.D(br32_1_busb), .en(bwrite), .Q(D), .clk(reloj), .clr(in_1));
  Register #(.width(5)) u_ES (.D(RW), .Q(ES_q), .clk(reloj), .clr(in_1));  // open: en
  Register #(.width(32)) IM (.D(bit_extender_1_out), .Q(IM_q), .clk(reloj), .clr(in_1));  // open: en
  Register #(.width(2)) register_7 (.D(muxw), .Q(register_7_q), .clk(reloj), .clr(in_1));  // open: en
  Register #(.width(5)) register_8 (.D(RB), .Q(register_8_q), .clk(reloj), .clr(in_1));  // open: en
  // Probe on adder_2_out
  Adder #(.width(32)) adder_2 (.a(A), .b(D), .out(adder_2_out));  // open: cin, cout
  // Probe on D
  // Probe on RC_q
  Register #(.width(32)) RC (.D(adder_2_out), .en(aluw), .Q(RC_q), .clk(reloj), .clr(in_1));
  // Probe on ram_1_data
  Register #(.width(1)) register_9 (.D(register_2_q), .Q(register_9_q), .clk(reloj), .clr(in_1));  // open: en
  Register #(.width(1)) register_10 (.D(register_3_q), .Q(noRW), .clk(reloj), .clr(in_1));  // open: en
  Register #(.width(1)) register_11 (.D(register_4_q), .Q(RM), .clk(reloj), .clr(in_1));  // open: en
  Register #(.width(1)) register_12 (.D(register_5_q), .Q(register_12_q), .clk(reloj), .clr(in_1));  // open: en
  Register #(.width(16)) register_13 (.D(A[15:0]), .Q(a_t), .clk(reloj), .clr(in_1));  // open: en
  Register #(.width(32)) register_14 (.D(D), .Q(d_t), .clk(reloj), .clr(in_1));  // open: en
  Register #(.width(5)) ES_2 (.D(ES_q), .Q(ES_2_q), .clk(reloj), .clr(in_1));  // open: en
  Register #(.width(32)) IM_2 (.D(IM_q), .Q(IM_2_q), .clk(reloj), .clr(in_1));  // open: en
  Register #(.width(2)) register_15 (.D(register_7_q), .Q(register_15_q), .clk(reloj), .clr(in_1));  // open: en
  Register #(.width(5)) register_16 (.D(register_8_q), .Q(register_16_q), .clk(reloj), .clr(in_1));  // open: en
  not not_4 (not_4_out, RM);
  // Probe on IM_2_q
  Register #(.width(1)) register_17 (.D(register_9_q), .Q(RegW), .clk(reloj), .clr(in_1));  // open: en
  Register #(.width(1)) register_18 (.D(noRW), .Q(muxpc), .clk(reloj), .clr(in_1));  // open: en
  Register #(.width(1)) register_19 (.D(register_12_q), .Q(muxb), .clk(reloj), .clr(in_1));  // open: en
  RAM #(.addrWidth(16), .dataWidth(32), .bus("separate")) ram_1 (
    .addr(a_t), .din(d_t), .data(ram_1_data), .str(not_4_out), .clk(reloj), .ld(RM), .clr(in_1));  // open: sel
  Register #(.width(5)) register_20 (.D(register_16_q), .Q(B), .clk(reloj), .clr(in_1));  // open: en
  Register #(.width(32)) register_21 (.D(RC_q), .Q(ALU), .clk(reloj), .clr(in_1));  // open: en
  Register #(.width(5)) ES_3 (.D(ES_2_q), .Q(ES), .clk(reloj), .clr(in_1));  // open: en
  Register #(.width(32)) IM_3 (.D(IM_2_q), .Q(INM), .clk(reloj), .clr(in_1));  // open: en
  Register #(.width(2)) register_22 (.D(register_15_q), .Q(MX), .clk(reloj), .clr(in_1));  // open: en

  // Other names for the same wires on the sheet: reset = in_1

  // Notes on the sheet:
  //   contents of rom_1 (hex, n*v repeats v):
  //   a00000a0 a0000040 a0002060 a0000020 a00420c0 a000c000 20000843 20000423 0 0 40000082 0 0 0 200014a4
  //   80026020 0 8000c000 0 a0000000 bfffe020 a009e040 a0096060 600000a0 800420c5 0 a009c080 a00400a0 0 0
  //   60000081 60000041 600000a1 60000041 60000061
  //   contents of rom_2 (hex, n*v repeats v):
  //   0 602 7ae 7ae 733 733 780 780 7c2 bc2 622 622
  //   código ASCII 7 bits a imprimir en tty (0 borra pantalla)
endmodule
