// Logisim project 735576-cache.circ as structural Verilog: 1 circuit, main circuit main
module main (
  input  in_1
);

  wire _1_out, _12_out, and_1_out, and_2_out, clock, clock_1_out, comparator_1_eq, comparator_2_eq,
       decoder_1_out0, decoder_1_out1, enW1, enW2, HIT, mem_en, not_1_out, not_2_out, not_3_out, not_4_out,
       REG_EN1, REG_EN2, REG_EN3, REG_EN4, shift_register_1_q23, viaE, viaL, WRITE;
  wire [0:0] ram_2_data, ram_3_data;
  wire [3:0] counter_1_q, WORD;
  wire [4:0] SET;
  wire [6:0] ram_2_data_2, ram_3_data_2, TAG;
  wire [23:0] counter_2_q;
  wire [31:0] _1, _2, _3, _4, BUS, multiplexer_1_out, multiplexer_2_out, multiplexer_3_out, ram_4_data,
       ram_5_data, ram_6_data, ram_7_data, ram_8_data, ram_9_data, ram_10_data, ram_11_data;

  not not_1 (not_1_out, viaE);
  not not_2 (not_2_out, HIT);
  Counter #(.width(4), .max('hb)) counter_1 (
    .count(not_2_out), .Q(counter_1_q), .clk(clock), .clr(not_3_out));  // open: load, D, carry
  not not_3 (not_3_out, not_2_out);
  Decoder #(.disabled(0)) decoder_1 (.out0(decoder_1_out0), .out1(decoder_1_out1), .sel(viaE), .en(and_1_out));
  RAM #(.addrWidth(5), .dataWidth(1), .bus("separate")) ram_1 (
    .addr(SET), .din(not_1_out), .data(viaE), .str(and_1_out), .clk(clock), .clr(in_1));  // open: sel, ld
  and and_1 (and_1_out, not_4_out, WRITE);
  Decoder #(.select(4), .disabled(0), .enable("false")) decoder_2 (
    .out4(REG_EN1), .out6(REG_EN2), .out8(REG_EN3), .out10(REG_EN4), .out11(WRITE), .sel(counter_1_q));  // open: out0, out1, out2, out3, out5, out7, out9, out12, out13, out14, out15
  not not_4 (not_4_out, HIT);
  Register #(.width(32)) register_1 (.D(BUS), .en(REG_EN1), .Q(_1), .clk(clock), .clr(in_1));
  Register #(.width(32)) register_2 (.D(BUS), .en(REG_EN2), .Q(_2), .clk(clock), .clr(in_1));
  Register #(.width(32)) register_3 (.D(BUS), .en(REG_EN3), .Q(_3), .clk(clock), .clr(in_1));
  Register #(.width(32)) register_4 (.D(BUS), .en(REG_EN4), .Q(_4), .clk(clock), .clr(in_1));
  RAM #(.addrWidth(5), .bus("separate")) ram_2 (
    .addr(SET), .din({TAG, 1'b1}), .data({ram_2_data_2, ram_2_data[0]}), .str(decoder_1_out0), .clk(clock),
    .clr(in_1));  // open: sel, ld
  Comparator #(.width(7)) comparator_1 (.a(ram_2_data_2), .b(TAG), .eq(comparator_1_eq));  // open: gt, lt
  and and_2 (and_2_out, ram_2_data[0], comparator_1_eq);
  or or_1 (HIT, and_2_out, viaL);
  RAM #(.addrWidth(5), .bus("separate")) ram_3 (
    .addr(SET), .din({TAG, 1'b1}), .data({ram_3_data_2, ram_3_data[0]}), .str(decoder_1_out1), .clk(clock),
    .clr(in_1));  // open: sel, ld
  and and_3 (viaL, ram_3_data[0], comparator_2_eq);
  Comparator #(.width(7)) comparator_2 (.a(ram_3_data_2), .b(TAG), .eq(comparator_2_eq));  // open: gt, lt
  not not_5 (mem_en, HIT);
  Button u__1 (.out(_1_out));
  Button _12 (.out(_12_out));
  Clock clock_1 (.out(clock_1_out));
  // MP_main MP: pin names not known; wires that end beside it: {TAG, SET, WORD}, mem_en, clock, BUS
  // Probe on BUS
  RAM #(.addrWidth(5), .dataWidth(32), .bus("separate")) ram_4 (
    .addr(SET), .din(_1), .data(ram_4_data), .str(enW1), .clk(clock), .clr(in_1));  // open: sel, ld
  Shift_Register #(.length(24)) shift_register_1 (
    .shift(1'b1), .in(1'b0), .clk(clock_1_out), .load(_12_out), .d0(1'b0), .d1(1'b1), .d2(1'b0), .d3(1'b1),
    .d4(1'b0), .d5(1'b1), .d6(1'b0), .d7(1'b1), .d8(1'b0), .d9(1'b1), .d10(1'b0), .d11(1'b1), .d12(1'b0),
    .d13(1'b1), .d14(1'b0), .d15(1'b1), .d16(1'b0), .d17(1'b1), .d18(1'b0), .d19(1'b1), .d20(1'b0),
    .d21(1'b1), .d22(1'b0), .d23(1'b1), .q23(shift_register_1_q23));  // open: out, clr, q0, q1, q2, q3, q4, q5, q6, q7, q8, q9, q10, q11, q12, q13, q14, q15, q16, q17, q18, q19, q20, q21, q22
  RAM #(.addrWidth(5), .dataWidth(32), .bus("separate")) ram_5 (
    .addr(SET), .din(_2), .data(ram_5_data), .str(enW1), .clk(clock), .clr(in_1));  // open: sel, ld
  Decoder #(.disabled(0)) decoder_3 (.out0(enW1), .out1(enW2), .sel(viaE), .en(WRITE));
  Counter #(.width(24), .max('hffffff)) counter_2 (
    .count(HIT), .Q(counter_2_q), .clk(clock), .clr(in_1));  // open: load, D, carry
  Multiplexer #(.select(2), .width(32), .enable("false")) multiplexer_1 (
    .in0(ram_4_data), .in1(ram_5_data), .in2(ram_6_data), .in3(ram_7_data), .out(multiplexer_1_out),
    .sel(WORD[3:2]));
  or or_2 (clock, _1_out, shift_register_1_q23);
  // Probe on multiplexer_1_out
  ROM #(.addrWidth(24), .dataWidth(16)) rom_1 (.addr(counter_2_q), .data({TAG, SET, WORD}));  // open: sel
  RAM #(.addrWidth(5), .dataWidth(32), .bus("separate")) ram_6 (
    .addr(SET), .din(_3), .data(ram_6_data), .str(enW1), .clk(clock), .clr(in_1));  // open: sel, ld
  RAM #(.addrWidth(5), .dataWidth(32), .bus("separate")) ram_7 (
    .addr(SET), .din(_4), .data(ram_7_data), .str(enW1), .clk(clock), .clr(in_1));  // open: sel, ld
  Multiplexer #(.width(32), .enable("false")) multiplexer_2 (
    .in0(multiplexer_1_out), .in1(multiplexer_3_out), .out(multiplexer_2_out), .sel(viaL));
  // Probe on multiplexer_2_out
  RAM #(.addrWidth(5), .dataWidth(32), .bus("separate")) ram_8 (
    .addr(SET), .din(_1), .data(ram_8_data), .str(enW2), .clk(clock), .clr(in_1));  // open: sel, ld
  // Probe on multiplexer_3_out
  RAM #(.addrWidth(5), .dataWidth(32), .bus("separate")) ram_9 (
    .addr(SET), .din(_2), .data(ram_9_data), .str(enW2), .clk(clock), .clr(in_1));  // open: sel, ld
  Multiplexer #(.select(2), .width(32), .enable("false")) multiplexer_3 (
    .in0(ram_8_data), .in1(ram_9_data), .in2(ram_10_data), .in3(ram_11_data), .out(multiplexer_3_out),
    .sel(WORD[3:2]));
  RAM #(.addrWidth(5), .dataWidth(32), .bus("separate")) ram_10 (
    .addr(SET), .din(_3), .data(ram_10_data), .str(enW2), .clk(clock), .clr(in_1));  // open: sel, ld
  RAM #(.addrWidth(5), .dataWidth(32), .bus("separate")) ram_11 (
    .addr(SET), .din(_4), .data(ram_11_data), .str(enW2), .clk(clock), .clr(in_1));  // open: sel, ld

  // Other names for the same wires on the sheet: reset = in_1

  // Notes on the sheet:
  //   UNIDAD DE CONTROL
  //   VIA 0
  //   VIA 1
  //   contents of rom_1 (hex, n*v repeats v):
  //   200 400 600 604 ed0 2d0 ad0 ad8 c608 b80c fe04 b804
endmodule
