// Logisim project 740246-cache.circ as structural Verilog: 1 circuit, main circuit main
module main (
  input  CLR,
  output [31:0] INST
);

  wire and_1_out, and_2_out, CLK, comparator_1_eq, comparator_2_eq, decoder_1_out0, decoder_1_out1, en0, en1,
       en2, en3, enW, enW1, enW2, hit, ld1, not_1_out, not_2_out, not_3_out, not_4_out, not_5_out, viaE, viaL;
  wire [3:0] counter_1_q;
  wire [7:0] ram_2_data, ram_3_data;
  wire [15:0] counter_2_q, DIR;
  wire [31:0] dato, multiplexer_1_out, multiplexer_3_out, ram_4_data, ram_5_data, ram_6_data, ram_7_data,
       ram_8_data, ram_9_data, ram_10_data, ram_11_data, w1, w2, w3, w4;

  Clock u_CLK (.out(CLK));
  not not_1 (not_1_out, viaE);
  not not_2 (not_2_out, hit);
  not not_3 (not_3_out, not_2_out);
  not not_4 (not_4_out, hit);
  and and_1 (and_1_out, not_4_out, enW);
  RAM #(.addrWidth(5), .dataWidth(1), .bus("separate")) ram_1 (
    .addr(DIR[8:4]), .din(not_1_out), .data(viaE), .str(and_1_out), .clk(CLK), .clr(CLR));  // open: sel, ld
  Counter #(.width(4), .max('hb)) counter_1 (
    .count(not_2_out), .Q(counter_1_q), .clk(CLK), .clr(not_3_out));  // open: load, D, carry
  Counter #(.width(16), .max('hffff)) counter_2 (
    .count(hit), .Q(counter_2_q), .clk(CLK), .clr(CLR));  // open: load, D, carry
  Decoder #(.disabled(0)) decoder_1 (.out0(decoder_1_out0), .out1(decoder_1_out1), .sel(viaE), .en(and_1_out));
  Decoder #(.select(4), .disabled(0), .enable("false")) decoder_2 (
    .out3(ld1), .out4(en0), .out6(en1), .out8(en2), .out10(en3), .out11(enW), .sel(counter_1_q));  // open: out0, out1, out2, out5, out7, out9, out12, out13, out14, out15
  RAM #(.addrWidth(5), .bus("separate")) ram_2 (
    .addr(DIR[8:4]), .din({DIR[15:9], 1'b1}), .data(ram_2_data), .str(decoder_1_out0), .clk(CLK), .clr(CLR));  // open: sel, ld
  RAM #(.addrWidth(5), .bus("separate")) ram_3 (
    .addr(DIR[8:4]), .din({DIR[15:9], 1'b1}), .data(ram_3_data), .str(decoder_1_out1), .clk(CLK), .clr(CLR));  // open: sel, ld
  ROM #(.addrWidth(16), .dataWidth(16)) rom_1 (.addr(counter_2_q), .data(DIR));  // open: sel
  Comparator #(.width(7)) comparator_1 (.a(ram_2_data[7:1]), .b(DIR[15:9]), .eq(comparator_1_eq));  // open: gt, lt
  Comparator #(.width(7)) comparator_2 (.a(ram_3_data[7:1]), .b(DIR[15:9]), .eq(comparator_2_eq));  // open: gt, lt
  not not_5 (not_5_out, hit);
  and and_2 (and_2_out, ram_2_data[0], comparator_1_eq);
  or or_1 (hit, and_2_out, viaL);
  and and_3 (viaL, ram_3_data[0], comparator_2_eq);
  // MP_main main_1: pin names not known; wires that end beside it: DIR, not_5_out, CLK, dato
  Register #(.width(32)) register_1 (.D(dato), .en(en0), .Q(w1), .clk(CLK), .clr(CLR));
  Register #(.width(32)) register_2 (.D(dato), .en(en1), .Q(w2), .clk(CLK), .clr(CLR));
  Register #(.width(32)) register_3 (.D(dato), .en(en2), .Q(w3), .clk(CLK), .clr(CLR));
  Register #(.width(32)) register_4 (.D(dato), .en(en3), .Q(w4), .clk(CLK), .clr(CLR));
  Decoder #(.disabled(0)) decoder_3 (.out0(enW1), .out1(enW2), .sel(viaE), .en(enW));
  RAM #(.addrWidth(5), .dataWidth(32), .bus("separate")) ram_4 (
    .addr(DIR[8:4]), .din(w1), .data(ram_4_data), .str(enW1), .clk(CLK), .clr(CLR));  // open: sel, ld
  RAM #(.addrWidth(5), .dataWidth(32), .bus("separate")) ram_5 (
    .addr(DIR[8:4]), .din(w2), .data(ram_5_data), .str(enW1), .clk(CLK), .clr(CLR));  // open: sel, ld
  RAM #(.addrWidth(5), .dataWidth(32), .bus("separate")) ram_6 (
    .addr(DIR[8:4]), .din(w3), .data(ram_6_data), .str(enW1), .clk(CLK), .clr(CLR));  // open: sel, ld
  RAM #(.addrWidth(5), .dataWidth(32), .bus("separate")) ram_7 (
    .addr(DIR[8:4]), .din(w4), .data(ram_7_data), .str(enW1), .clk(CLK), .clr(CLR));  // open: sel, ld
  RAM #(.addrWidth(5), .dataWidth(32), .bus("separate")) ram_8 (
    .addr(DIR[8:4]), .din(w1), .data(ram_8_data), .str(enW2), .clk(CLK), .clr(CLR));  // open: sel, ld
  RAM #(.addrWidth(5), .dataWidth(32), .bus("separate")) ram_9 (
    .addr(DIR[8:4]), .din(w2), .data(ram_9_data), .str(enW2), .clk(CLK), .clr(CLR));  // open: sel, ld
  RAM #(.addrWidth(5), .dataWidth(32), .bus("separate")) ram_10 (
    .addr(DIR[8:4]), .din(w3), .data(ram_10_data), .str(enW2), .clk(CLK), .clr(CLR));  // open: sel, ld
  RAM #(.addrWidth(5), .dataWidth(32), .bus("separate")) ram_11 (
    .addr(DIR[8:4]), .din(w4), .data(ram_11_data), .str(enW2), .clk(CLK), .clr(CLR));  // open: sel, ld
  Multiplexer #(.select(2), .width(32), .enable("false")) multiplexer_1 (
    .in0(ram_4_data), .in1(ram_5_data), .in2(ram_6_data), .in3(ram_7_data), .out(multiplexer_1_out),
    .sel(DIR[3:2]));
  Multiplexer #(.width(32), .enable("false")) multiplexer_2 (
    .in0(multiplexer_1_out), .in1(multiplexer_3_out), .out(INST), .sel(viaL));
  Multiplexer #(.select(2), .width(32), .enable("false")) multiplexer_3 (
    .in0(ram_8_data), .in1(ram_9_data), .in2(ram_10_data), .in3(ram_11_data), .out(multiplexer_3_out),
    .sel(DIR[3:2]));

  // Other names for the same wires on the sheet: WORD[1:0] = DIR[3:2]; SET[4:0] = DIR[8:4]; TAG[6:0] = DIR[15:9]

  // Notes on the sheet:
  //   SEÑALES
  //   GESTIÓN DE ETIQUETAS
  //   UNIDAD DE CONTROL
  //   LANZADOR DE DIRECCIONES
  //   contents of rom_1 (hex, n*v repeats v):
  //   200 400 600 404 9a0 ba0 da0 ba8 e04 6404 5804 580c
  //   MEMORIA PRINCIPAL
  //   GESTIÓN DE DATOS
endmodule
