// Logisim project clk_gen.circ as structural Verilog: 1 circuit, main circuit clk_gen
module clk_gen (
);

  wire _1_out, _12_out, clock_1_out, or_1_out, shift_register_1_q23;

  Button _1 (.out(_1_out));
  Button _12 (.out(_12_out));
  Shift_Register #(.length(24)) shift_register_1 (
    .shift(1'b1), .in(1'b0), .clk(clock_1_out), .load(_12_out), .d0(1'b0), .d1(1'b1), .d2(1'b0), .d3(1'b1),
    .d4(1'b0), .d5(1'b1), .d6(1'b0), .d7(1'b1), .d8(1'b0), .d9(1'b1), .d10(1'b0), .d11(1'b1), .d12(1'b0),
    .d13(1'b1), .d14(1'b0), .d15(1'b1), .d16(1'b0), .d17(1'b1), .d18(1'b0), .d19(1'b1), .d20(1'b0),
    .d21(1'b1), .d22(1'b0), .d23(1'b1), .q23(shift_register_1_q23));  // open: out, clr, q0, q1, q2, q3, q4, q5, q6, q7, q8, q9, q10, q11, q12, q13, q14, q15, q16, q17, q18, q19, q20, q21, q22
  Clock clock_1 (.out(clock_1_out));
  or or_1 (or_1_out, _1_out, shift_register_1_q23);

  // Notes on the sheet:
  //   Instrucciones de uso del generador de reloj:
  //   - Abre este archivo en la misma instancia de logisim
  //   - Pulsa ctrl-k para empezar a simular
  //   - Usa los botones para generar 1 o 12 pulsos de reloj
  //   - Copia y pega en tu circuito y conecta la salida de la OR a tu señal de reloj
endmodule
